// Logisim project clase.circ as structural Verilog: 1 circuit, main circuit main
module main (
  input  in_1,
  input  in_2,
  input  in_3,
  input  in_4,
  input  in_5,
  output out_6,
  output out_7,
  output out_8,
  output out_9,
  output out_10
);

  or or_1 (out_10, in_5, in_5);
  nand nand_1 (out_6, in_2, out_7);
  nand nand_2 (out_7, out_6, in_1);
  nor nor_1 (out_8, in_4, out_9);
  nor nor_2 (out_9, out_8, in_3);
endmodule
