// Logisim project ej13.circ as structural Verilog: 1 circuit, main circuit main
module main (
  input  in_1,
  input  in_2,
  input  in_3,
  input  in_4,
  input  in_5,
  input  in_6,
  input  in_7,
  input  in_8,
  input  in_9,
  input  in_10,
  input  in_11,
  input  in_12,
  output out_13,
  output out_14,
  output out_15,
  output out_16,
  output out_17,
  output out_18,
  output out_19,
  output out_20,
  output out_21,
  output out_22,
  output out_23,
  output out_24,
  output out_25
);

  wire and_1_out, and_2_out, and_3_out, and_4_out, not_5_out, not_6_out, not_7_out, not_8_out, not_10_out,
       not_11_out, not_12_out, not_13_out, not_15_out;

  not not_1 (out_13, in_1);
  not not_2 (out_16, in_4);
  not not_3 (out_17, in_7);
  not not_4 (out_20, in_8);
  not not_5 (not_5_out, in_2);
  not not_6 (not_6_out, in_5);
  not not_7 (not_7_out, in_9);
  not not_8 (not_8_out, in_11);
  xor xor_1 (out_21, not_7_out, not_8_out);
  not not_9 (out_23, not_8_out);
  and and_1 (and_1_out, not_8_out, not_7_out);
  and and_2 (and_2_out, and_1_out, not_6_out);
  xor xor_2 (out_18, not_6_out, and_1_out);
  xor xor_3 (out_14, not_5_out, and_2_out);
  not not_10 (not_10_out, in_3);
  not not_11 (not_11_out, in_6);
  not not_12 (not_12_out, in_10);
  not not_13 (not_13_out, in_12);
  and and_3 (and_3_out, not_13_out, not_12_out);
  xor xor_4 (out_22, not_12_out, not_13_out);
  not not_14 (out_24, not_13_out);
  xor xor_5 (out_19, not_11_out, and_3_out);
  xor xor_6 (out_15, not_10_out, and_4_out);
  and and_4 (and_4_out, and_3_out, not_11_out);
  not not_15 (not_15_out, out_15);
  and and_5 (out_25, not_15_out, in_12);
endmodule
