// Logisim project prueba_latch_d.circ as structural Verilog: 1 circuit, main circuit main
module main (
  input  in_1,
  input  in_2,
  input  in_3,
  input  in_4,
  output out_5,
  output out_6,
  output out_7,
  output out_8
);

  wire and_1_out, and_2_out, nand_1_out, nand_2_out, not_1_out, undriven;

  nand nand_1 (nand_1_out, in_1, in_3);
  nand nand_2 (nand_2_out, nand_1_out, in_3);
  nand nand_3 (out_5, nand_1_out, out_7);
  nand nand_4 (out_7, out_5, nand_2_out);
  not not_1 (not_1_out, in_2);
  and and_1 (and_1_out, in_2, in_4);
  and and_2 (and_2_out, in_4, not_1_out);
  nor nor_1 (out_6, and_2_out, undriven);
  nor nor_2 (out_8, out_6, and_1_out);
endmodule
